// Logisim project ALU.circ as structural Verilog: 7 circuits, main circuit main
module main (
  input  A4,
  input  A3,
  input  A2,
  input  A1,
  input  B4,
  input  B3,
  input  B2,
  input  B1,
  input  CS2,
  input  CS1,
  input  CS0,
  output S4,
  output S3,
  output S2,
  output S1,
  output S,
  output Z,
  output V,
  output C
);

  wire a_pr_1_y1, a_pr_1_y2, a_pr_1_y3, a_pr_1_y4, b_pr_1_y1, b_pr_1_y2, b_pr_1_y3, b_pr_1_y4,
       logic_circuit_1_y1, logic_circuit_1_y2, logic_circuit_1_y3, logic_circuit_1_y4, n7402_1__1__1y,
       n7402_1__4__2y, n7402_1__13__4y, n7404_1__2__1y, n7404_1__4__2y, n7432_1__3__1y, n7432_1__6__2y,
       n7432_1__8__3y, n7432_1__11__4y, n7483_1__2__s3, n7483_1__6__s2, n7483_1__9__s1, n7483_1__14__cout,
       n7483_1__15__s4, n7486_1__3__1y, n7486_1__6__2y, n7486_1__8__3y;

  _7404 u_7404_1 (
    ._1__1A(CS0), ._2__1Y(n7404_1__2__1y), ._3__2A(CS1), ._4__2Y(n7404_1__4__2y), ._13__6A(n7432_1__8__3y),
    ._12__6Y(Z));  // open: _5__3A, _6__3Y, _7__GND, _14__Vcc, _11__5A, _10__5Y, _9__4A, _8__4Y
  _7402 u_7402_1 (
    ._1__1Y(n7402_1__1__1y), ._2__1A(CS2), ._3__1B(n7404_1__2__1y), ._4__2Y(n7402_1__4__2y), ._5__2A(CS0),
    ._6__2B(CS2), ._13__4Y(n7402_1__13__4y), ._12__4B(CS2), ._11__4A(CS1));  // open: _7__GND, _14__Vcc, _10__3Y, _9__3B, _8__3A
  LOGIC_CIRCUIT logic_circuit_1 (
    .SELECTOR(CS0), .A4(A4), .A3(A3), .A2(A2), .A1(A1), .B4(B4), .B3(B3), .B2(B2), .B1(B1),
    .Y4(logic_circuit_1_y4), .Y3(logic_circuit_1_y3), .Y2(logic_circuit_1_y2), .Y1(logic_circuit_1_y1));
  A_PR a_pr_1 (
    .XOR_BIT(n7402_1__4__2y), .A4(A4), .A3(A3), .A2(A2), .A1(A1), .Y4(a_pr_1_y4), .Y3(a_pr_1_y3),
    .Y2(a_pr_1_y2), .Y1(a_pr_1_y1));
  B_PR b_pr_1 (
    .SELECTOR(n7402_1__1__1y), .CONST(CS2), .XOR_BIT(n7404_1__4__2y), .B4(B4), .B3(B3), .B2(B2), .B1(B1),
    .Y4(b_pr_1_y4), .Y3(b_pr_1_y3), .Y2(b_pr_1_y2), .Y1(b_pr_1_y1));
  _7483 u_7483_1 (
    ._1__A4(a_pr_1_y4), ._2__S3(n7483_1__2__s3), ._3__A3(a_pr_1_y3), ._4__B3(b_pr_1_y3), ._5__Vcc(1'b1),
    ._6__S2(n7483_1__6__s2), ._7__B2(b_pr_1_y2), ._8__A2(a_pr_1_y2), ._16__B4(b_pr_1_y4),
    ._15__S4(n7483_1__15__s4), ._14__Cout(n7483_1__14__cout), ._13__Cin(n7402_1__13__4y), ._12__GND(1'b0),
    ._11__B1(b_pr_1_y1), ._10__A1(a_pr_1_y1), ._9__S1(n7483_1__9__s1));
  _7432 u_7432_1 (
    ._1__1A(n7404_1__4__2y), ._2__1B(n7402_1__1__1y), ._3__1Y(n7432_1__3__1y), ._4__2A(S1), ._5__2B(S2),
    ._6__2Y(n7432_1__6__2y), ._13__4B(n7432_1__6__2y), ._12__4A(S3), ._11__4Y(n7432_1__11__4y),
    ._10__3B(n7432_1__11__4y), ._9__3A(S), ._8__3Y(n7432_1__8__3y));  // open: _7__GND, _14__Vcc
  _7486 u_7486_1 (
    ._1__1A(a_pr_1_y4), ._2__1B(b_pr_1_y4), ._3__1Y(n7486_1__3__1y), ._4__2A(n7486_1__3__1y),
    ._5__2B(n7483_1__14__cout), ._6__2Y(n7486_1__6__2y), ._10__3B(S), ._9__3A(n7486_1__6__2y),
    ._8__3Y(n7486_1__8__3y));  // open: _7__GND, _14__Vcc, _13__4B, _12__4A, _11__4Y
  _4_BIT_2X1_MUX u_4_bit_2x1_mux_1 (
    .A4(logic_circuit_1_y4), .A3(logic_circuit_1_y3), .A2(logic_circuit_1_y2), .A1(logic_circuit_1_y1),
    .L4(n7483_1__15__s4), .L3(n7483_1__2__s3), .L2(n7483_1__6__s2), .L1(n7483_1__9__s1),
    .SELECTOR(n7432_1__3__1y), .Y4(S), .Y3(S3), .Y2(S2), .Y1(S1));
  _74157 u_74157_1 (
    ._1__S(n7432_1__3__1y), ._2__A1(1'b0), ._3__B1(n7486_1__8__3y), ._4__Y1(V), ._5__A2(1'b0),
    ._6__B2(n7483_1__14__cout), ._7__Y2(C), ._8__GND(1'b0), ._15__G(1'b0));  // open: _16__Vcc, _14__A4, _13__B4, _12__Y4, _11__A3, _10__B3, _9__Y3

  assign S4 = S;
endmodule

module _4_BIT_XOR (
  input  A4,
  input  A3,
  input  A2,
  input  A1,
  input  B4,
  input  B3,
  input  B2,
  input  B1,
  output Y4,
  output Y3,
  output Y2,
  output Y1
);

  _7486 u_7486_1 (
    ._1__1A(A4), ._2__1B(B4), ._3__1Y(Y4), ._4__2A(A3), ._5__2B(B3), ._6__2Y(Y3), ._13__4B(A2), ._12__4A(B2),
    ._11__4Y(Y2), ._10__3B(A1), ._9__3A(B1), ._8__3Y(Y1));  // open: _7__GND, _14__Vcc
endmodule

module _4_BIT_AND (
  input  A4,
  input  A3,
  input  A2,
  input  A1,
  input  B4,
  input  B3,
  input  B2,
  input  B1,
  output Y4,
  output Y3,
  output Y2,
  output Y1
);

  _7408 u_7408_1 (
    ._1__1A(A4), ._2__1B(B4), ._3__1Y(Y4), ._4__2A(A3), ._5__2B(B3), ._6__2Y(Y3), ._13__4B(A2), ._12__4A(B2),
    ._11__4Y(Y2), ._10__3B(A1), ._9__3A(B1), ._8__3Y(Y1));  // open: _7__GND, _14__Vcc
endmodule

// LOGICAL
module LOGIC_CIRCUIT (
  input  SELECTOR,
  input  A4,
  input  A3,
  input  A2,
  input  A1,
  input  B4,
  input  B3,
  input  B2,
  input  B1,
  output Y4,
  output Y3,
  output Y2,
  output Y1
);

  wire AND_y1, AND_y2, AND_y3, AND_y4, XOR_y1, XOR_y2, XOR_y3, XOR_y4;

  _4_BIT_XOR XOR (
    .A4(A4), .A3(A3), .A2(A2), .A1(A1), .B4(B4), .B3(B3), .B2(B2), .B1(B1), .Y4(XOR_y4), .Y3(XOR_y3),
    .Y2(XOR_y2), .Y1(XOR_y1));
  _4_BIT_AND AND (
    .A4(A4), .A3(A3), .A2(A2), .A1(A1), .B4(B4), .B3(B3), .B2(B2), .B1(B1), .Y4(AND_y4), .Y3(AND_y3),
    .Y2(AND_y2), .Y1(AND_y1));
  _74157 u_74157_1 (
    ._1__S(SELECTOR), ._2__A1(XOR_y4), ._3__B1(AND_y4), ._4__Y1(Y4), ._5__A2(XOR_y3), ._6__B2(AND_y3),
    ._7__Y2(Y3), ._15__G(1'b0), ._14__A4(XOR_y2), ._13__B4(AND_y2), ._12__Y4(Y2), ._11__A3(XOR_y1),
    ._10__B3(AND_y1), ._9__Y3(Y1));  // open: _8__GND, _16__Vcc
endmodule

// X_i
module A_PR (
  input  XOR_BIT,
  input  A4,
  input  A3,
  input  A2,
  input  A1,
  output Y4,
  output Y3,
  output Y2,
  output Y1
);

  _4_BIT_XOR u_4_bit_xor_1 (
    .A4(A4), .A3(A3), .A2(A2), .A1(A1), .B4(XOR_BIT), .B3(XOR_BIT), .B2(XOR_BIT), .B1(XOR_BIT), .Y4(Y4),
    .Y3(Y3), .Y2(Y2), .Y1(Y1));
endmodule

// Y_i
module B_PR (
  input  SELECTOR,
  input  CONST,
  input  XOR_BIT,
  input  B4,
  input  B3,
  input  B2,
  input  B1,
  output Y4,
  output Y3,
  output Y2,
  output Y1
);

  wire n4_bit_xor_1_y1, n4_bit_xor_1_y2, n4_bit_xor_1_y3, n4_bit_xor_1_y4;

  _4_BIT_XOR u_4_bit_xor_1 (
    .A4(XOR_BIT), .A3(XOR_BIT), .A2(XOR_BIT), .A1(XOR_BIT), .B4(B4), .B3(B3), .B2(B2), .B1(B1),
    .Y4(n4_bit_xor_1_y4), .Y3(n4_bit_xor_1_y3), .Y2(n4_bit_xor_1_y2), .Y1(n4_bit_xor_1_y1));
  _74157 u_74157_1 (
    ._1__S(SELECTOR), ._2__A1(CONST), ._3__B1(n4_bit_xor_1_y4), ._4__Y1(Y4), ._5__A2(CONST),
    ._6__B2(n4_bit_xor_1_y3), ._7__Y2(Y3), ._15__G(1'b0), ._14__A4(CONST), ._13__B4(n4_bit_xor_1_y2),
    ._12__Y4(Y2), ._11__A3(CONST), ._10__B3(n4_bit_xor_1_y1), ._9__Y3(Y1));  // open: _8__GND, _16__Vcc
endmodule

module _4_BIT_2X1_MUX (
  input  A4,
  input  A3,
  input  A2,
  input  A1,
  input  L4,
  input  L3,
  input  L2,
  input  L1,
  input  SELECTOR,
  output Y4,
  output Y3,
  output Y2,
  output Y1
);

  _74157 u_74157_1 (
    ._1__S(SELECTOR), ._2__A1(A4), ._3__B1(L4), ._4__Y1(Y4), ._5__A2(A3), ._6__B2(L3), ._7__Y2(Y3),
    ._8__GND(1'b0), ._16__Vcc(1'b1), ._15__G(1'b0), ._14__A4(A2), ._13__B4(L2), ._12__Y4(Y2), ._11__A3(A1),
    ._10__B3(L1), ._9__Y3(Y1));
endmodule
