// Logisim project fpadder.circ as structural Verilog: 5 circuits, main circuit main
module main (
  input  [31:0] A,
  input  [31:0] B,
  output [21:0] Sum,
  output [18:0] Truncated_fraction,
  output [31:0] Output
);

  wire [11:0] shift_compare_1_exponent;
  wire [12:0] adder_2_out, nomalizer_1_shift_amount;
  wire [12:12] subtractor_1_out;
  wire [21:0] complementer_1_output, shift_compare_1_larger, shift_compare_1_smaller;

  shift_compare shift_compare_1 (
    .Larger(shift_compare_1_larger), .Smaller(shift_compare_1_smaller), .Exponent(shift_compare_1_exponent),
    .A(B), .B(A));
  Adder #(.width(22)) adder_1 (
    .a(shift_compare_1_larger), .b(shift_compare_1_smaller), .out(Sum), .cin(1'b0));  // open: cout
  Adder #(.width(13)) adder_2 (
    .a({1'b0, shift_compare_1_exponent}), .b(13'h2), .out(adder_2_out), .cin(1'b0));  // open: cout
  Subtractor #(.width(13)) subtractor_1 (
    .a(adder_2_out), .b(nomalizer_1_shift_amount), .out({subtractor_1_out[12], Output[30:19]}), .bin(1'b0));  // open: bout
  complementer complementer_1 (.Input(Sum), .Sign_bit(Sum[21]), .Output(complementer_1_output), .Sign(Output[31]));
  nomalizer nomalizer_1 (
    .Input(complementer_1_output), .Shift_amount(nomalizer_1_shift_amount), .Truncated(Output[18:0]));  // open: Zero

  assign Truncated_fraction = Output[18:0];
endmodule

module complementer (
  input  [21:0] Input,
  input  Sign_bit,
  output [21:0] Output,
  output Sign
);

  wire [21:0] negator_1_out;

  Negator #(.width(22)) negator_1 (.in(Input), .out(negator_1_out));
  Multiplexer #(.width(22), .disabled(0), .enable("false")) multiplexer_1 (
    .in0(Input), .in1(negator_1_out), .out(Output), .sel(Sign_bit));

  assign Sign = Sign_bit;
endmodule

module exp_compare (
  input  [11:0] X,
  input  [11:0] Y,
  output X____Y,
  output X___Y,
  output [4:0] Difference,
  output [11:0] Larger
);

  wire comparator_1_eq, comparator_1_gt, comparator_2_gt;
  wire [11:0] multiplexer_1_out, subtractor_1_out;
  wire [11:5] multiplexer_3_out;

  Comparator #(.width(12), .mode("unsigned")) comparator_1 (
    .a(X), .b(Y), .gt(comparator_1_gt), .eq(comparator_1_eq), .lt(X___Y));
  or or_1 (X____Y, comparator_1_gt, comparator_1_eq);
  Multiplexer #(.width(12), .disabled(0), .enable("false")) multiplexer_1 (
    .in0(X), .in1(Y), .out(multiplexer_1_out), .sel(X____Y));
  Multiplexer #(.width(12), .disabled(0), .enable("false")) multiplexer_2 (.in0(X), .in1(Y), .out(Larger), .sel(X___Y));
  Subtractor #(.width(12)) subtractor_1 (
    .a(Larger), .b(multiplexer_1_out), .out(subtractor_1_out), .bin(1'b0));  // open: bout
  Comparator #(.width(12), .mode("unsigned")) comparator_2 (
    .a(subtractor_1_out), .b(12'h1f), .gt(comparator_2_gt));  // open: eq, lt
  Multiplexer #(.width(12), .disabled(0), .enable("false")) multiplexer_3 (
    .in0(subtractor_1_out), .in1(12'h1f), .out({multiplexer_3_out, Difference}), .sel(comparator_2_gt));
endmodule

module shift_compare (
  input  [31:0] A,
  input  [31:0] B,
  output [21:0] Larger,
  output [21:0] Smaller,
  output [11:0] Exponent
);

  wire exp_compare_1_x____y, exp_compare_1_x___y;
  wire [4:0] exp_compare_1_difference;
  wire [21:0] complementer_1_output, complementer_2_output, multiplexer_1_out;

  exp_compare exp_compare_1 (
    .X(A[30:19]), .Y(B[30:19]), .X____Y(exp_compare_1_x____y), .X___Y(exp_compare_1_x___y),
    .Difference(exp_compare_1_difference), .Larger(Exponent));
  complementer complementer_1 (
    .Input({3'b001, A[18:0]}), .Sign_bit(A[31]), .Output(complementer_1_output));  // open: Sign
  Multiplexer #(.width(22), .disabled(0), .enable("false")) multiplexer_1 (
    .in0(complementer_1_output), .in1(complementer_2_output), .out(multiplexer_1_out),
    .sel(exp_compare_1_x____y));
  Shifter #(.width(22), .shift("ar")) shifter_1 (
    .in(multiplexer_1_out), .\dist (exp_compare_1_difference), .out(Smaller));
  Multiplexer #(.width(22), .disabled(0), .enable("false")) multiplexer_2 (
    .in0(complementer_1_output), .in1(complementer_2_output), .out(Larger), .sel(exp_compare_1_x___y));
  complementer complementer_2 (
    .Input({3'b001, B[18:0]}), .Sign_bit(B[31]), .Output(complementer_2_output));  // open: Sign
endmodule

module nomalizer (
  input  [21:0] Input,
  output [12:0] Shift_amount,
  output [18:0] Truncated,
  output Zero
);

  wire bitfinder_1_found;
  wire [21:0] shifter_1_out;

  BitFinder #(.width(22)) bitfinder_1 (
    .in({Input[0], Input[1], Input[2], Input[3], Input[4], Input[5], Input[6], Input[7], Input[8], Input[9], Input[10], Input[11], Input[12], Input[13], Input[14], Input[15], Input[16], Input[17], Input[18], Input[19], Input[20], 1'b0}),
    .index(Shift_amount[4:0]), .found(bitfinder_1_found));
  Shifter #(.width(22)) shifter_1 (
    .in(Input), .\dist (Shift_amount[4:0]), .out({shifter_1_out[21], Truncated, shifter_1_out[1:0]}));
  not not_1 (Zero, bitfinder_1_found);

  assign Shift_amount[12:5] = {8{1'b0}};
endmodule
